# Fritzing sketch sketch (saved by Fritzing 0.9.3b)
breadboards: 1

parts:
  Part1 = Arduino Uno (Rev3)
  Part2 = Bluetooth HC-05 Macho
  R1 = Resistor [tolerance=±5% resistance=220 package=THT]
  LED1 = LED - 5mm [color="Red (633nm)" package="5 mm [THT]"]

nets:
  N1: Part1.D10_PWM/SS, Part2.RXD
  N2: Part1.D11_PWM/MOSI, Part2.TXD
  GND: Part1.GND, Part2.GND, R1.Pin_1
  N3: Part1.D6_PWM, LED1.anode
  5V: Part1.5V, Part2.VCC
  N4: R1.Pin_0, LED1.cathode
